# Fritzing sketch ToiletIoT (saved by Fritzing 0.9.3b)

parts:
  U1 = lolin
  Q1 = NPN-Transistor [package="TO92 [THT]"]
  J1 = Piezo Speaker
  S1 = Reed switch [package=THT]
  R1 = Resistor [tolerance=±5% resistance=100 package=THT]

nets:
  N1: U1.connector0, J1.pin2
  N2: U1.connector5, S1.pin_1
  N3: U1.connector15, S1.pin_2
  N4: U1.connector28, R1.Pin_1
  N5: U1.connector37, Q1.E
  N6: Q1.B, R1.Pin_0
  N7: Q1.C, J1.pin1
